# Fritzing sketch project (saved by Fritzing 0.9.3b)

parts:
  Part1 = Arduino Uno (Rev3)
  LED1 = LED - 5mm [color="Red (633nm)" package="5 mm [THT]"]
  R1 = Resistor [tolerance=±5% resistance=220 package="0603 [SMD]"]

nets:
  N1: Part1.GND, LED1.cathode
  N2: Part1.D2, R1.Pin_1
  N3: LED1.anode, R1.Pin_0

// code stored in the sketch: project.ino
#define BLYNK_TEMPLATE_ID "TMPL3CgpjdhN7"
#define BLYNK_TEMPLATE_NAME "Home Automation"
#define BLYNK_AUTH_TOKEN "x7jy_3ChLkYzZ-zZaPOr4wagSn81BgGp"


#define BLYNK_PRINT Serial


#include <WiFi.h>
#include <BlynkSimpleEsp32.h>


char ssid[] = "PRASAD_5G";
char pass[] = "8686327059";


// Define the pin for the LED
const int ledPin = 2;  // You can change the pin number as per your setup


void setup() {
  // Debug console
  Serial.begin(9600);


  // Set the LED pin as an output
  pinMode(ledPin, OUTPUT);


  // Connect to Wi-Fi
  WiFi.begin(ssid, pass);
  while (WiFi.status() != WL_CONNECTED) {
    delay(500);
    Serial.print(".");
  }
  Serial.println("WiFi connected");


  // Connect to Blynk
  Blynk.begin(BLYNK_AUTH_TOKEN, ssid, pass);
}


void loop() {
  Blynk.run();
}


// BLYNK_WRITE is a function that gets called every time a value is written to the virtual pin V1 from the Blynk app
BLYNK_WRITE(V1) {
  int pinValue = param.asInt(); // Get value as integer


  if (pinValue == 1) {
    digitalWrite(ledPin, HIGH);  // Turn LED on
  } else {
    digitalWrite(ledPin, LOW);   // Turn LED off
  }
}
